// Logisim project BNN.circ as structural Verilog: 9 circuits, main circuit MatrixMultiply_Module
module MatrixMultiply_Module (
  input  CLK,
  input  RST,
  input  Start_MatMul,
  input  W_Data_In,
  input  Im2Col_Data_In,
  output Output_Write_Enable,
  output [3:0] Output_Data,
  output [8:0] Im2Col_Addr,
  output [8:0] Weight_Addr,
  output [10:0] Output_Write_Addr,
  output MatMul_Done
);

  wire Carry1, Carry2, comparator_1_eq, comparator_2_eq, comparator_4_eq, d_ff_1_q, d_ff_2_q, d_ff_3_q,
       not_1_out, xnor_1_out, xor_1_out;
  wire [3:0] adder_4_out, bit_extender_7_out, DPC, multiplexer_1_out, register_1_q;
  wire [4:0] row_counter_q;
  wire [5:0] col_counter_q;
  wire [8:0] bit_extender_2_out, bit_extender_3_out, bit_extender_4_out, CC, multiplier_1_out,
       multiplier_2_out;
  wire [10:0] adder_3_out, bit_extender_5_out, bit_extender_6_out, multiplier_3_out;

  D_Flip_Flop d_ff_1 (.D(Carry1), .clk(CLK), .Q(d_ff_1_q));  // open: Qn, preset, reset
  xor xor_1 (xor_1_out, Start_MatMul, MatMul_Done);
  D_Flip_Flop d_ff_2 (.D(Carry2), .clk(CLK), .Q(d_ff_2_q));  // open: Qn, preset, reset
  not not_1 (not_1_out, xor_1_out);
  Counter #(.max('h8), .width(4)) dot_prod_counter (
    .clr(not_1_out), .clk(CLK), .carry(Carry1), .Q(DPC));  // open: load, up, count, D
  Counter #(.max('h23), .width(6)) col_counter (
    .clr(RST), .clk(d_ff_1_q), .carry(Carry2), .Q(col_counter_q));  // open: load, up, count, D
  Counter #(.max('h1f), .width(5)) row_counter (
    .clr(RST), .clk(d_ff_2_q), .Q(row_counter_q));  // open: load, up, count, D, carry
  assign CC = {{3{1'b0}}, col_counter_q};  // Bit_Extender bit_extender_1
  assign bit_extender_2_out = {{4{1'b0}}, row_counter_q};  // Bit_Extender bit_extender_2
  Multiplier #(.width(9)) multiplier_1 (.a(CC), .b(9'h9), .out(multiplier_1_out));  // open: cin, cout
  Multiplier #(.width(9)) multiplier_2 (.a(bit_extender_2_out), .b(9'h9), .out(multiplier_2_out));  // open: cin, cout
  Comparator #(.width(9)) comparator_1 (.a(CC), .b(9'h23), .eq(comparator_1_eq));  // open: gt, lt
  Comparator #(.width(5)) comparator_2 (.a(row_counter_q), .b({5{1'b1}}), .eq(comparator_2_eq));  // open: gt, lt
  assign bit_extender_3_out = {{5{1'b0}}, DPC};  // Bit_Extender bit_extender_3
  assign bit_extender_4_out = {{5{1'b0}}, DPC};  // Bit_Extender bit_extender_4
  assign bit_extender_5_out = {{2{1'b0}}, CC};  // Bit_Extender bit_extender_5
  Register #(.width(4)) register_1 (.D(DPC), .clk(CLK), .Q(register_1_q), .clr(RST));  // open: en
  Adder #(.width(9)) adder_1 (.a(bit_extender_3_out), .b(multiplier_1_out), .out(Im2Col_Addr));  // open: cin, cout
  Adder #(.width(9)) adder_2 (.a(bit_extender_4_out), .b(multiplier_2_out), .out(Weight_Addr));  // open: cin, cout
  assign bit_extender_6_out = {{2{1'b0}}, multiplier_2_out};  // Bit_Extender bit_extender_6
  and and_1 (MatMul_Done, comparator_1_eq, comparator_2_eq);
  Multiplier #(.width(11)) multiplier_3 (.a(bit_extender_6_out), .b(11'h4), .out(multiplier_3_out));  // open: cin, cout
  Comparator #(.width(4)) comparator_3 (.a(register_1_q), .b(4'b1000), .eq(Output_Write_Enable));  // open: gt, lt
  Adder #(.width(11)) adder_3 (.a(bit_extender_5_out), .b(multiplier_3_out), .out(adder_3_out));  // open: cin, cout
  D_Flip_Flop d_ff_3 (.D(Output_Write_Enable), .clk(CLK), .Q(d_ff_3_q), .reset(RST));  // open: Qn, preset
  Register #(.width(11)) register_2 (.D(adder_3_out), .en(d_ff_3_q), .clk(CLK), .Q(Output_Write_Addr), .clr(RST));
  Register #(.width(4)) Accumulator_Reg (.D(adder_4_out), .clk(CLK), .Q(Output_Data), .clr(RST));  // open: en
  assign bit_extender_7_out = {{3{1'b0}}, xnor_1_out};  // Bit_Extender bit_extender_7
  xnor xnor_1 (xnor_1_out, W_Data_In, Im2Col_Data_In);
  Adder #(.width(4)) adder_4 (.a(multiplexer_1_out), .b(bit_extender_7_out), .out(adder_4_out));  // open: cin, cout
  Multiplexer #(.width(4)) multiplexer_1 (
    .in0(Output_Data), .in1(4'b0000), .out(multiplexer_1_out), .sel(comparator_4_eq));
  Comparator #(.width(4)) comparator_4 (.a(4'b0000), .b(DPC), .eq(comparator_4_eq));  // open: gt, lt

  // Other names for the same wires on the sheet: En = Output_Write_Enable; MD = MatMul_Done
endmodule

module Scaling_GAP_Module (
  input  CLK,
  input  RST,
  input  [4:0] Data_In,
  input  StartGAP,
  output [7:0] Output_Data,
  output GAP_Done,
  output Output_EN,
  output [6:0] Output_Vector_Addr,
  output [10:0] RAM_Read_Addr,
  output [1:0] RAM_Mux_Select
);

  wire Acc_clr, comparator_2_lt, d_ff_2_q, not_1_out, PCC, T, xor_1_out;
  wire [5:0] Pixel_Counter_q;
  wire [7:0] bit_extender_1_out, bit_extender_4_out, multiplier_1_out;
  wire [10:0] bit_extender_3_out, bit_extender_5_out, multiplier_2_out;
  wire [12:0] adder_1_out, bit_extender_2_out, multiplexer_1_out, register_1_q, shifter_1_out;

  xor xor_1 (xor_1_out, StartGAP, GAP_Done);
  assign bit_extender_1_out = {{3{Data_In[4]}}, Data_In};  // Bit_Extender bit_extender_1
  not not_1 (not_1_out, xor_1_out);
  Multiplier #(.mode("twosComplement")) multiplier_1 (
    .a(bit_extender_1_out), .b(8'ha), .out(multiplier_1_out));  // open: cin, cout
  D_Flip_Flop d_ff_1 (.D(T), .clk(CLK), .Q(Output_EN));  // open: Qn, preset, reset
  Multiplexer #(.width(13)) multiplexer_1 (
    .in0(register_1_q), .in1({13{1'b0}}), .out(multiplexer_1_out), .sel(Acc_clr));
  assign bit_extender_2_out = {{5{multiplier_1_out[7]}}, multiplier_1_out};  // Bit_Extender bit_extender_2
  Counter #(.max('h23), .width(6)) Pixel_Counter (
    .clr(not_1_out), .clk(CLK), .carry(T), .Q(Pixel_Counter_q));  // open: load, up, count, D
  Adder #(.width(13)) adder_1 (.a(multiplexer_1_out), .b(bit_extender_2_out), .out(adder_1_out));  // open: cin, cout
  Register #(.width(13)) register_1 (.D(adder_1_out), .clk(CLK), .Q(register_1_q), .clr(RST));  // open: en
  assign bit_extender_3_out = {{5{1'b0}}, Pixel_Counter_q};  // Bit_Extender bit_extender_3
  Comparator #(.mode("unsigned"), .width(6)) comparator_1 (
    .a(Pixel_Counter_q), .b({6{1'b0}}), .eq(Acc_clr));  // open: gt, lt
  D_Flip_Flop d_ff_2 (.D(T), .clk(CLK), .Q(d_ff_2_q));  // open: Qn, preset, reset
  D_Flip_Flop d_ff_3 (.D(d_ff_2_q), .clk(CLK), .Q(PCC));  // open: Qn, preset, reset
  Bit_Extender #(.in_width(13), .out_width(8)) bit_extender_4 (.in(shifter_1_out), .out(bit_extender_4_out));
  Shifter #(.shift("lr"), .width(13)) shifter_1 (.in(register_1_q), .\dist (4'b0101), .out(shifter_1_out));
  Counter #(.max('h7f), .width(7)) Channel_Counter (
    .clr(RST), .clk(PCC), .carry(GAP_Done), .Q(Output_Vector_Addr));  // open: load, up, count, D
  Multiplexer #(.width(8)) multiplexer_2 (
    .in0(bit_extender_4_out), .in1({8{1'b1}}), .out(Output_Data), .sel(comparator_2_lt));
  Comparator comparator_2 (.a(bit_extender_4_out), .b({8{1'b1}}), .lt(comparator_2_lt));  // open: gt, eq
  assign bit_extender_5_out = {{6{1'b0}}, Output_Vector_Addr[4:0]};  // Bit_Extender bit_extender_5
  Multiplier #(.width(11)) multiplier_2 (
    .a(bit_extender_5_out), .b(11'h24), .out(multiplier_2_out));  // open: cin, cout
  Adder #(.width(11)) adder_2 (.a(multiplier_2_out), .b(bit_extender_3_out), .out(RAM_Read_Addr));  // open: cin, cout

  assign RAM_Mux_Select = Output_Vector_Addr[6:5];

  // Other names for the same wires on the sheet: GD = GAP_Done; T2 = Output_EN
endmodule

module BinaryFC_Module (
  input  Start_FC,
  input  CLK,
  input  RST,
  input  [7:0] Vector_Data_In,
  input  W_Data_In,
  output [10:0] FC_ROM_Read_Addr,
  output [6:0] GAP_RAM_Read_Addr,
  output Done,
  output [3:0] Predicted_digit
);

  wire CLK_t, comparator_1_eq, d_ff_1_q, d_ff_2_q, d_ff_3_q, d_ff_4_q, demultiplexer_1_out10, En, NCC,
       not_3_out, not_4_out, RE0, RE1, RE2, RE3, RE4, RE5, RE6, RE7, RE8, RE9, register_1_q, S, Sign3,
       Sub32_Sign, Sub32_Sign2, undriven, xor_1_out;
  wire [3:0] argmax_counter_q, NC, register_3_q, register_4_q;
  wire [7:0] adder_1_out, multiplexer_1_out, not_1_out;
  wire [10:0] bit_extender_2_out, bit_extender_3_out, shifter_1_out;
  wire [14:0] Acc, adder_2_out, bit_extender_1_out, Max_value_reg_q, multiplexer_3_out, N0, N1, N2, N3, N4,
       N5, N6, N7, N8, N9, Neuron;

  Register #(.width(1)) register_1 (.D(W_Data_In), .clk(CLK_t), .Q(register_1_q), .clr(RST));  // open: en
  Clock clock_1 (.out(CLK_t));
  assign not_1_out = ~Vector_Data_In;  // NOT_Gate not_1, 8 bits wide
  buf xor_1 (xor_1_out, Done);  // XOR_Gate
  // NOT_Gate not_2 has open pins: in=xor_1_out, out=open
  Adder adder_1 (.a(8'h1), .b(not_1_out), .out(adder_1_out), .cin(1'b0));  // open: cout
  Multiplexer #(.width(8)) multiplexer_1 (
    .in0(adder_1_out), .in1(Vector_Data_In), .out(multiplexer_1_out), .sel(register_1_q));
  Counter #(.max('h7f), .width(7)) DPC (
    .clr(not_3_out), .clk(CLK_t), .carry(S), .Q(GAP_RAM_Read_Addr));  // open: load, up, count, D
  not not_3 (not_3_out, Start_FC);
  assign bit_extender_1_out = {{7{multiplexer_1_out[7]}}, multiplexer_1_out};  // Bit_Extender bit_extender_1
  Adder #(.width(15)) adder_2 (.a(Acc), .b(bit_extender_1_out), .out(adder_2_out), .cin(1'b0));  // open: cout
  D_Flip_Flop d_ff_1 (.D(S), .clk(CLK_t), .Q(d_ff_1_q));  // open: Qn, preset, reset
  not not_4 (not_4_out, comparator_1_eq);
  Comparator #(.mode("unsigned"), .width(4)) comparator_1 (.a(NC), .b(4'b0000), .eq(comparator_1_eq));  // open: gt, lt
  Register #(.width(15)) register_2 (.D(adder_2_out), .clk(CLK_t), .Q(Neuron), .clr(RST));  // open: en
  D_Flip_Flop d_ff_2 (.D(S), .clk(CLK_t), .Q(d_ff_2_q), .reset(RST));  // open: Qn, preset
  D_Flip_Flop d_ff_3 (.D(d_ff_2_q), .clk(CLK_t), .Q(d_ff_3_q), .reset(RST));  // open: Qn, preset
  Register #(.width(4)) register_3 (.D(NC), .clk(CLK_t), .Q(register_3_q), .clr(RST));  // open: en
  assign bit_extender_2_out = {{4{1'b0}}, GAP_RAM_Read_Addr};  // Bit_Extender bit_extender_2
  Comparator #(.width(7)) comparator_2 (.a(GAP_RAM_Read_Addr), .b({7{1'b1}}), .eq(Sub32_Sign));  // open: gt, lt
  Comparator #(.mode("unsigned"), .width(7)) comparator_3 (
    .a(GAP_RAM_Read_Addr), .b({7{1'b0}}), .gt(Sub32_Sign2), .eq(Sign3));  // open: lt
  Multiplexer #(.width(15)) multiplexer_2 (.in0(Neuron), .in1({15{1'b0}}), .out(Acc), .sel(Sign3));
  Register #(.width(4)) register_4 (.D(register_3_q), .clk(CLK_t), .Q(register_4_q), .clr(RST));  // open: en
  Counter #(.max('h9), .width(4)) u_NC (.clr(RST), .clk(d_ff_1_q), .carry(NCC), .Q(NC));  // open: load, up, count, D
  D_Flip_Flop d_ff_4 (.clk(CLK_t), .Q(d_ff_4_q), .reset(RST));  // open: D, Qn, preset
  Counter #(.max('h9), .width(4)) argmax_counter (
    .clr(RST), .clk(d_ff_3_q), .carry(Done), .Q(argmax_counter_q));  // open: load, up, count, D
  Demultiplexer #(.select(4)) demultiplexer_1 (
    .out0(RE0), .out1(RE1), .out2(RE2), .out3(RE3), .out4(RE4), .out5(RE5), .out6(RE6), .out7(RE7),
    .out8(RE8), .out9(RE9), .out10(demultiplexer_1_out10), .in(Sign3), .sel(register_4_q));  // open: out11, out12, out13, out14, out15
  assign bit_extender_3_out = {{7{1'b0}}, NC};  // Bit_Extender bit_extender_3
  Register #(.width(15)) register_5 (.D(Neuron), .clk(RE0), .Q(N0), .clr(RST));  // open: en
  Register #(.width(15)) register_6 (.D(Neuron), .clk(RE3), .Q(N3), .clr(RST));  // open: en
  Register #(.width(15)) register_7 (.D(Neuron), .clk(RE6), .Q(N6), .clr(RST));  // open: en
  Register #(.width(15)) register_8 (.D(Neuron), .clk(RE9), .Q(N9), .clr(RST));  // open: en
  Shifter #(.width(11)) shifter_1 (.in(bit_extender_3_out), .\dist (4'b0111), .out(shifter_1_out));
  Adder #(.width(11)) adder_3 (.a(shifter_1_out), .b(bit_extender_2_out), .out(FC_ROM_Read_Addr));  // open: cin, cout
  Register #(.width(15)) register_9 (.D(Neuron), .en(undriven), .clk(RE1), .Q(N1), .clr(RST));
  Register #(.width(15)) register_10 (.D(Neuron), .clk(RE4), .Q(N4), .clr(RST));  // open: en
  Register #(.width(15)) register_11 (.D(Neuron), .clk(RE7), .Q(N7), .clr(RST));  // open: en
  Register #(.width(4)) Max_index_reg (.D(argmax_counter_q), .clk(En), .Q(Predicted_digit), .clr(RST));  // open: en
  Register #(.width(15)) register_12 (.D(Neuron), .clk(RE2), .Q(N2), .clr(RST));  // open: en
  Register #(.width(15)) register_13 (.D(Neuron), .clk(RE5), .Q(N5), .clr(RST));  // open: en
  Register #(.width(15)) register_14 (.D(Neuron), .clk(RE8), .Q(N8), .clr(RST));  // open: en
  Multiplexer #(.select(4), .width(15)) multiplexer_3 (
    .in0(N0), .in1(N1), .in2(N2), .in3(N3), .in4(N4), .in5(N5), .in6(N6), .in7(N7), .in8(N8), .in9(N9),
    .out(multiplexer_3_out), .sel(argmax_counter_q));  // open: in10, in11, in12, in13, in14, in15
  Register #(.width(15)) Max_value_reg (.D(multiplexer_3_out), .clk(En), .Q(Max_value_reg_q), .clr(RST));  // open: en
  Comparator #(.width(15)) comparator_4 (.a(Max_value_reg_q), .b(multiplexer_3_out), .lt(En));  // open: gt, eq
endmodule

module Control_FSM (
  input  Global_Start,
  input  CLK,
  input  MatMul_Done,
  input  GAP_Done,
  input  FC_Argmax_Done,
  input  RST,
  output Start_Matmul,
  output Start_ScalingGAP,
  output Start_FC_Argmax,
  output System_Done
);

  wire [2:0] fsm_logic_1_ns0, register_1_q;

  Register #(.width(3)) register_1 (.D(fsm_logic_1_ns0), .clk(CLK), .Q(register_1_q), .clr(RST));  // open: en
  FSM_logic fsm_logic_1 (
    .CS2(register_1_q[2]), .CS1(register_1_q[1]), .CS0(register_1_q[0]), .Global_Start(Global_Start),
    .MatMul_Done(MatMul_Done), .GAP_Done(GAP_Done), .FC_Argmax_Done(FC_Argmax_Done),
    .NS2(fsm_logic_1_ns0[2]), .NS1(fsm_logic_1_ns0[1]), .NS0(fsm_logic_1_ns0[0]),
    .Start_Matmul(Start_Matmul), .Start_ScalingGAP(Start_ScalingGAP), .Start_FC_Argmax(Start_FC_Argmax),
    .System_Done(System_Done));
endmodule

module FSM_logic (
  input  CS2,
  input  CS1,
  input  CS0,
  input  Global_Start,
  input  MatMul_Done,
  input  GAP_Done,
  input  FC_Argmax_Done,
  output NS2,
  output NS1,
  output NS0,
  output Start_Matmul,
  output Start_ScalingGAP,
  output Start_FC_Argmax,
  output System_Done
);

  wire and_1_out, and_2_out, and_3_out, and_4_out, and_5_out, and_6_out, and_7_out, and_8_out, not_1_out,
       not_2_out, not_3_out, not_4_out, not_5_out;

  not not_1 (not_1_out, CS2);
  not not_2 (not_2_out, CS1);
  not not_3 (not_3_out, CS0);
  not not_4 (not_4_out, MatMul_Done);
  not not_5 (not_5_out, FC_Argmax_Done);
  and and_1 (and_1_out, CS1, CS0, FC_Argmax_Done);
  and and_2 (and_2_out, not_2_out, CS0, MatMul_Done);
  and and_3 (and_3_out, not_1_out, CS1, not_3_out);
  and and_4 (and_4_out, not_1_out, CS1, not_5_out);
  and and_5 (and_5_out, not_1_out, not_2_out, not_3_out, Global_Start);
  and and_6 (and_6_out, not_2_out, CS0, not_4_out);
  and and_7 (and_7_out, not_1_out, CS1, not_3_out, GAP_Done);
  and and_8 (and_8_out, CS1, CS0, not_5_out);
  and and_9 (Start_Matmul, not_2_out, CS0);
  and and_10 (Start_ScalingGAP, not_1_out, CS1, not_3_out);
  and and_11 (Start_FC_Argmax, CS1, CS0);
  or or_1 (NS2, CS2, and_1_out);
  or or_2 (NS1, and_2_out, and_3_out, and_4_out);
  or or_3 (NS0, and_5_out, and_6_out, and_7_out, and_8_out);

  assign System_Done = CS2;
endmodule

module Activation_Module (
  input  [3:0] Data_In,
  output [4:0] Data_Out
);

  ROM #(.addrWidth(4), .dataWidth(5)) rom_1 (.addr(Data_In), .data(Data_Out));

  // Notes on the sheet:
  //   contents of rom_1 (hex, n*v repeats v):
  //   5*1f 1 3 5 7 9
endmodule

module TestModule (
  input  [7:0] in_1,
  input  rst,
  input  [7:0] in_3,
  input  [7:0] in_4,
  input  [7:0] in_5,
  input  in_6,
  input  in_7,
  input  in_8,
  input  in_9,
  input  in_10,
  input  in_11,
  input  in_12,
  input  in_13
);

  wire clock_1_out, counter_1_carry, d_ff_1_q;

  Counter #(.max('h3), .width(2)) counter_1 (
    .clr(rst), .clk(clock_1_out), .carry(counter_1_carry));  // open: load, up, count, D, Q
  Clock clock_1 (.out(clock_1_out));
  D_Flip_Flop d_ff_1 (.D(counter_1_carry), .Q(d_ff_1_q));  // open: clk, Qn, preset, reset
  Counter #(.max('h1), .width(1)) counter_2 (.clk(d_ff_1_q));  // open: clr, load, up, count, D, carry, Q
endmodule

module Quantized_CNN (
  input  CLK,
  input  Global_Start,
  input  Global_Reset,
  output CNN_Done,
  output [3:0] Digit
);

  wire CLK_t, D, GD, im2col, M0_output_write_enable, M1_output_write_enable, M2_output_write_enable,
       M3_output_write_enable, MD, MD0, MD1, MD2, MD3, scaling_gap_module_1_output_en, SFC, SFC2, SM, SSG,
       W2, Weights0, Weights1, Weights2, Weights3;
  wire [1:0] RAM_Mux_Sel;
  wire [3:0] Data_In0, Data_In1, Data_In2, Data_In3, M0_output_data, M1_output_data, M2_output_data,
       M3_output_data;
  wire [4:0] activation_module_1_data_out, activation_module_2_data_out, activation_module_3_data_out,
       activation_module_4_data_out, Data_In;
  wire [6:0] GRRA, multiplexer_6_out, scaling_gap_module_1_output_vector_addr;
  wire [7:0] scaling_gap_module_1_output_data, Vector_Data;
  wire [8:0] Im2col_A, W_A;
  wire [10:0] FCRA, M0_output_write_addr, M1_output_write_addr, M2_output_write_addr, M3_output_write_addr,
       multiplexer_1_out, multiplexer_2_out, multiplexer_3_out, multiplexer_4_out, SG_Addr;

  Clock clock_1 (.out(CLK_t));
  Control_FSM control_fsm_1 (
    .Global_Start(Global_Start), .CLK(CLK_t), .MatMul_Done(MD), .GAP_Done(GD), .FC_Argmax_Done(D),
    .RST(Global_Reset), .Start_Matmul(SM), .Start_ScalingGAP(SSG), .Start_FC_Argmax(SFC),
    .System_Done(CNN_Done));
  MatrixMultiply_Module M0 (
    .CLK(CLK_t), .RST(Global_Reset), .Start_MatMul(SM), .W_Data_In(Weights0), .Im2Col_Data_In(im2col),
    .Output_Write_Enable(M0_output_write_enable), .Output_Data(M0_output_data), .Im2Col_Addr(Im2col_A),
    .Weight_Addr(W_A), .Output_Write_Addr(M0_output_write_addr), .MatMul_Done(MD0));
  MatrixMultiply_Module M1 (
    .CLK(CLK_t), .RST(Global_Reset), .Start_MatMul(SM), .W_Data_In(Weights1), .Im2Col_Data_In(im2col),
    .Output_Write_Enable(M1_output_write_enable), .Output_Data(M1_output_data), .Weight_Addr(W_A),
    .Output_Write_Addr(M1_output_write_addr), .MatMul_Done(MD1));  // open: Im2Col_Addr
  MatrixMultiply_Module M2 (
    .CLK(CLK_t), .RST(Global_Reset), .Start_MatMul(SM), .W_Data_In(Weights2), .Im2Col_Data_In(im2col),
    .Output_Write_Enable(M2_output_write_enable), .Output_Data(M2_output_data), .Weight_Addr(W_A),
    .Output_Write_Addr(M2_output_write_addr), .MatMul_Done(MD2));  // open: Im2Col_Addr
  MatrixMultiply_Module M3 (
    .CLK(CLK_t), .RST(Global_Reset), .Start_MatMul(SM), .W_Data_In(Weights3), .Im2Col_Data_In(im2col),
    .Output_Write_Enable(M3_output_write_enable), .Output_Data(M3_output_data), .Weight_Addr(W_A),
    .Output_Write_Addr(M3_output_write_addr), .MatMul_Done(MD3));  // open: Im2Col_Addr
  ROM #(.addrWidth(9), .dataWidth(1)) Im2col_ROM (.addr(Im2col_A));  // open: data
  ROM #(.addrWidth(11), .dataWidth(1)) FC_Weights_ROM (.addr(FCRA));  // open: data
  ROM #(.addrWidth(9), .dataWidth(1)) conv1_W_ROM (.addr(W_A));  // open: data
  ROM #(.addrWidth(9), .dataWidth(1)) rom_1 (.addr(W_A));  // open: data
  Multiplexer #(.width(11)) multiplexer_1 (
    .in0(M0_output_write_addr), .in1(SG_Addr), .out(multiplexer_1_out), .sel(SSG));
  RAM #(.addrWidth(11), .dataWidth(4)) Conv1_Output_RAM (
    .addr(multiplexer_1_out), .we(M0_output_write_enable), .oe(SSG), .clk(CLK_t), .din(M0_output_data),
    .dout(Data_In0));
  Multiplexer #(.width(11)) multiplexer_2 (
    .in0(M1_output_write_addr), .in1(SG_Addr), .out(multiplexer_2_out), .sel(SSG));
  RAM #(.addrWidth(11), .dataWidth(4)) ram_1 (
    .addr(multiplexer_2_out), .we(M1_output_write_enable), .oe(SSG), .clk(CLK_t), .din(M1_output_data),
    .dout(Data_In1));
  Multiplexer #(.width(11)) multiplexer_3 (
    .in0(M2_output_write_addr), .in1(SG_Addr), .out(multiplexer_3_out), .sel(SSG));
  RAM #(.addrWidth(11), .dataWidth(4)) ram_2 (
    .addr(multiplexer_3_out), .we(M2_output_write_enable), .oe(SSG), .clk(CLK_t), .din(M2_output_data),
    .dout(Data_In2));
  Multiplexer #(.width(11)) multiplexer_4 (
    .in0(M3_output_write_addr), .in1(SG_Addr), .out(multiplexer_4_out), .sel(SSG));
  RAM #(.addrWidth(11), .dataWidth(4)) ram_3 (
    .addr(multiplexer_4_out), .we(M3_output_write_enable), .oe(SSG), .clk(CLK_t), .din(M3_output_data),
    .dout(Data_In3));
  ROM #(.addrWidth(9), .dataWidth(1)) rom_2 (.addr(W_A));  // open: data
  ROM #(.addrWidth(9), .dataWidth(1)) rom_3 (.addr(W_A));  // open: data
  and and_1 (MD, MD0, MD1, MD2, MD3);
  Activation_Module activation_module_1 (.Data_In(Data_In0), .Data_Out(activation_module_1_data_out));
  Activation_Module activation_module_2 (.Data_In(Data_In1), .Data_Out(activation_module_2_data_out));
  Activation_Module activation_module_3 (.Data_In(Data_In2), .Data_Out(activation_module_3_data_out));
  Activation_Module activation_module_4 (.Data_In(Data_In3), .Data_Out(activation_module_4_data_out));
  Multiplexer #(.select(2), .width(5)) multiplexer_5 (
    .in0(activation_module_1_data_out), .in1(activation_module_2_data_out),
    .in2(activation_module_3_data_out), .in3(activation_module_4_data_out), .out(Data_In), .sel(RAM_Mux_Sel));
  Scaling_GAP_Module scaling_gap_module_1 (
    .CLK(CLK_t), .RST(Global_Reset), .Data_In(Data_In), .StartGAP(SSG),
    .Output_Data(scaling_gap_module_1_output_data), .GAP_Done(GD),
    .Output_EN(scaling_gap_module_1_output_en), .Output_Vector_Addr(scaling_gap_module_1_output_vector_addr),
    .RAM_Read_Addr(SG_Addr), .RAM_Mux_Select(RAM_Mux_Sel));
  RAM #(.addrWidth(7)) ram_4 (
    .addr(multiplexer_6_out), .we(scaling_gap_module_1_output_en), .oe(SFC2), .clk(CLK_t),
    .din(scaling_gap_module_1_output_data), .dout(Vector_Data));
  Multiplexer #(.width(7)) multiplexer_6 (
    .in0(scaling_gap_module_1_output_vector_addr), .in1(GRRA), .out(multiplexer_6_out), .sel(SFC2));
  D_Flip_Flop d_ff_1 (.D(SFC), .clk(CLK_t), .Q(SFC2));  // open: Qn, preset, reset
  BinaryFC_Module binaryfc_module_1 (
    .Start_FC(SFC), .CLK(CLK_t), .RST(Global_Reset), .Vector_Data_In(Vector_Data), .W_Data_In(W2),
    .FC_ROM_Read_Addr(FCRA), .GAP_RAM_Read_Addr(GRRA), .Done(D), .Predicted_digit(Digit));
  Hex_Digit_Display hex_digit_display_1 (.value(Digit));  // open: dp

  // Other names for the same wires on the sheet: RST = Global_Reset

  // Notes on the sheet:
  //   contents of Im2col_ROM (hex, n*v repeats v):
  //   5*0 1 0 0 1 0 0 1 0 0 1 5*0 1 37*0 1 1 0 1 0 0 1 1 0 1 5*0 1 37*0 4*1 0 0 4*1 5*0 1 38*0 1 1 1 0 0
  //   4*1 0 0 1 0 0 1 0 0 1 0 0 1 0 0 1 0 0 1 0 0 1 0 0 1 0 0 1 0 0 1 0 0 1 0 0 1 0 0 1 6*0 1 1 0 0 1 0 1
  //   1 0 0 1 0 0 1 0 0 1 0 0 1 0 0 1 0 0 1 0 0 1 0 0 1 0 0 1 0 0 1 0 0 1 0 0 1 0 0 1 7*0 1 0 0 1 0 0 1 0
  //   0 1 0 0 1 0 0 1 0 0 1 0 0 1 0 0 1 0 0 1 0 0 1 0 0 1 0 0 1 0 0 1 0 0 1 0 0 1
  //   contents of FC_Weights_ROM (hex, n*v repeats v):
  //   5*1 0 0 1 1 0 0 0 1 1 4*0 1 1 0 5*1 0 1 1 0 1 1 1 0 0 0 1 0 0 0 1 5*0 1 0 0 1 1 1 0 0 1 4*0 1 0 1 0
  //   1 1 1 0 1 0 0 1 0 0 1 1 0 4*1 0 1 1 0 4*1 0 0 1 1 1 0 4*1 4*0 1 0 1 0 1 1 0 7*1 0 1 1 0 0 1 0 0 0 1
  //   0 0 1 0 1 8*0 1 0 0 1 0 0 4*1 0 4*1 0 1 0 4*1 0 0 0 4*1 0 0 4*1 0 1 0 5*1 0 0 1 0 0 0 1 1 0 1 1 1 0
  //   1 0 0 1 0 0 1 0 0 1 0 1 1 0 0 0 1 1 0 1 0 4*1 0 1 1 0 0 1 1 1 0 0 0 1 0 1 0 1 0 6*1 0 1 0 0 0 1 0 0
  //   1 0 1 1 0 1 0 1 1 1 0 1 1 0 0 5*1 0 1 0 1 1 1 0 4*1 0 1 0 0 1 0 1 0 4*1 0 0 1 1 1 0 1 1 0 4*1 0 1 1
  //   0 1 0 1 0 1 1 5*0 1 10*0 1 1 5*0 1 1 4*0 1 1 0 1 0 0 0 1 0 1 1 0 0 1 0 7*1 0 1 0 1 0 0 1 1 0 0 1 1 0
  //   1 0 4*1 0 0 1 1 1 0 0 0 1 1 1 0 1 1 0 1 1 1 0 1 0 0 1 0 1 1 0 1 0 4*1 0 0 1 0 1 0 1 0 1 1 1 0 1 1 0
  //   0 1 0 1 1 0 1 0 1 1 0 1 1 1 0 1 1 0 1 1 5*0 1 0 1 1 0 0 1 1 1 5*0 1 0 0 1 1 1 4*0 1 0 0 1 0 0 1 1 0
  //   0 1 0 1 0 0 1 0 1 1 1 0 4*1 0 0 1 1 0 0 0 1 4*0 1 1 0 1 0 1 0 1 1 0 1 1 0 0 0 1 0 1 1 1 0 1 0 1 1 0
  //   1 0 1 0 1 1 0 0 1 1 1 4*0 1 1 0 0 0 1 1 0 1 0 1 1 0 0 5*1 0 1 0 1 1 0 1 0 4*1 0 1 0 1 1 1 0 0 1 0 1
  //   0 1 0 4*1 0 0 0 1 4*0 1 0 1 1 1 0 0 1 0 1 1 0 1 0 5*1 0 4*1 4*0 1 0 0 4*1 0 1 1 0 1 1 0 1 1 0 1 1 0
  //   4*1 0 1 1 0 0 0 1 0 1 0 1 1 0 1 1 0 1 1 0 1 0 1 0 0 1 0 1 0 1 0 5*1 0 1 1 0 0 1 1 1 0 0 1 0 1 7*0 1
  //   1 1 0 0 0 1 0 1 1 0 0 0 1 1 1 0 0 1 0 1 1 0 1 1 1 0 1 1 0 0 1 1 0 0 1 0 0 0 1 0 1 0 0 1 0 0 1 0 0 0
  //   1 0 1 1 1 0 1 1 0 0 4*1 0 1 1 0 4*1 0 1 1 1 0 0 1 1 0 1 1 0 0 0 1 1 0 1 1 0 1 0 6*1 0 1 0 0 1 0 0 1
  //   1 1 0 0 1 1 0 1 0 0 4*1 0 1 1 0 0 1 1 0 0 1 1 1 0 1 0 0 0 1 0 1 0 1 0 1 0 1 1 1 0 1 1 5*0 1 0 0 1 1
  //   1 0 1 1 0 1 4*0 1 0 1 0 1 0 1 0 1 1 1 0 1 0 1 0 5*1 0 1 1 0 1 0 1 1 0 0 1 0 1 0 0 4*1 0 0 0 1 0 6*1
  //   0 0 1 1 0 1 0 1 0 0 0 1 1 5*0 1 0 0 1 0 0 1 0 1 1 0 1 4*0 1 1 1 0 0 0 1 0 0 1 1 1 0 1 1 0 1 0 5*1 0
  //   1 1 0 0 1 1 0 0 1 1 1 0 1 1 1 0 0 1 0 0 5*1 0 1 1 1 0 0 0 1 1 0 1 0 1 1 0 0 6*1 5*0 1 0 0 4*1 0 1 1
  //   0 1 0 1 1 1 0 1 0 0 1 0 1 0 0 1 0 1 0 1 0 1 1 0 1 1 0 0 1 0 11*1 4*0 6*1 0 1 1 0 1 0 1 0 7*1 0 1 1 0
  //   1 0 1 1 0 0 0 4*1 0 1 0 0 1 1 0 0 1 0 1 1 1 0 0 1 0 1 0 1 1 0 1 0 0 1 1 0 0 0 1 0 1 0 1 1 0 1 1 1 0
  //   0 1 1 0 1 1 1 0 0 1 1 0 1 1 1 0 0 1 1 0 0 0 5*1 0 1 0 1 0 0 0 1 1 0 1 1 0 0 0 1 1 0 1 1 0 1 0 1 1 0
  //   1 0 1 0 0 1 0 1 1 0 1 1 1 0 1 0 1 0 1 0 0 0 1 0 4*1 0 1 0 1 0 1
  //   contents of conv1_W_ROM (hex, n*v repeats v):
  //   1 0 1 1 1 0 1 0 1 1 1 0 1 1 1 0 0 1 0 1 1 1 0 0 4*1 0 0 1 0 6*1 0 0 1 1 0 1 0 1 0 1 1 0 0 0 7*1 0 0
  //   4*1 0 1 0 1 1 0 1 0 0 5*1 0 1 1 1 0 5*1 0 1 1 1 0 1 1 0 1 0 4*1 0 0 1 1 0 1 0 0 1 0 1 1 1 0 1 1 1 0
  //   0 1 1 0 1 0 1 0 1 0 1 0 5*1 0 0 0 4*1 0 0 4*1 0 1 0 1 0 0 7*1 0 0 0 1 0 5*1 0 1 1 0 0 1 0 0 6*1 0 0
  //   1 0 5*1 0 0 0 5*1 0 1 0 6*1 0 1 0 0 0 8*1 0 1 1 0 1 0 5*1 0 1 0 1 0 0 1 0 1 0 1 1 0 1 1 1 0 1 1 0 0
  //   1 1 0 1 0 5*1 0 1 0 1 1 1 0 1 0 5*1 0 1 1
  //   contents of rom_1 (hex, n*v repeats v):
  //   0 1 1 0 0 1 1 0 5*1 0 1 0 0 1 0 1 1 1 0 1 0 5*1 0 1 1 1 0 0 1 0 1 1 1 0 5*1 0 0 0 1 1 0 1 1 0 0 1 0
  //   6*1 0 1 0 0 1 1 4*0 8*1 0 1 1 0 0 1 1 0 5*1 0 1 0 4*1 0 1 0 1 0 4*1 0 7*1 0 1 1 0 1 1 1 0 1 1 0 0 0
  //   1 1 0 1 1 1 0 1 0 6*1 0 0 1 1 1 0 0 5*1 0 5*1 0 0 1 0 1 0 1 0 4*1 0 1 1 0 1 0 1 1 1 0 0 0 1 1 0 1 0
  //   1 0 1 0 1 0 0 5*1 0 5*1 0 0 4*1 0 1 1 1 0 1 0 1 0 1 0 5*1 0 8*1 0 0 4*1 0 1 0 0 4*1 0 1 1 1 0 1 0 1
  //   0 1 0 1 0 1 1 0 0 8*1 0 1 1 1
  //   contents of rom_2 (hex, n*v repeats v):
  //   6*1 0 0 0 1 1 1 0 0 0 1 1 1 0 0 1 1 1 0 4*1 0 1 0 1 1 1 0 0 0 1 0 1 1 0 1 0 4*1 0 1 1 0 1 1 1 0 4*1
  //   0 1 0 6*1 0 0 0 1 0 1 0 1 1 1 0 6*1 0 1 0 1 1 0 0 1 1 1 0 1 1 1 0 0 4*1 0 0 1 1 0 1 0 4*1 0 0 1 1 0
  //   0 0 6*1 0 1 1 0 0 1 1 0 1 1 1 0 4*1 0 0 1 1 1 4*0 1 0 4*1 0 1 1 0 1 1 0 1 0 1 0 1 1 0 1 0 1 1 0 14*1
  //   0 1 1 0 0 1 1 1 0 0 0 1 1 1 0 1 1 1 0 0 1 0 1 1 0 1 1 0 1 0 4*1 0 0 1 0 1 0 6*1 0 0 1 1 0 0 0 1 1 1
  //   0 1 1 1 0 1 0 1 0 1 1 1 0 7*1 0 1 1 1 0 1 1 1 0 1 1 1 4*0 1 1
  //   contents of rom_3 (hex, n*v repeats v):
  //   1 1 1 0 1 1 0 1 0 0 1 1 0 1 1 1 0 0 0 1 1 0 1 1 0 0 1 1 0 0 0 8*1 0 0 1 0 1 0 0 0 4*1 0 6*1 0 1 1 0
  //   0 4*1 0 1 1 0 1 1 1 0 4*1 0 0 6*1 0 1 0 0 1 1 0 0 0 4*1 0 1 0 1 0 1 1 0 1 1 1 0 4*1 0 1 0 1 0 1 1 0
  //   6*1 0 0 1 0 1 1 1 0 0 1 0 1 1 0 1 1 0 0 1 0 0 12*1 0 1 1 0 1 1 0 0 1 1 0 0 1 1 1 0 1 1 1 0 1 1 0 7*1
  //   0 1 1 0 0 1 0 5*1 0 0 1 1 0 0 1 1 0 5*1 0 0 4*1 0 0 0 1 1 1 0 1 1 1 0 6*1 0 5*1 0 1 1 0 1 1 0 5*1 0
  //   1 0 0 5*1 0 1 0 1 1 0 1 1 0 1 1 0 1 0 0 1 1 1
endmodule

module Image_CNN (
);

  Quantized_CNN quantized_cnn_1 ();  // open: CLK, Global_Start, Global_Reset, CNN_Done, Digit
endmodule
